# Fritzing sketch ultrasonic-range (saved by Fritzing 0.9.1b)
breadboards: 1

parts:
  Part1 = Arduino Uno (Rev3)
  Part2 = SRF05 Ultrasonic Rangefinder

nets:
  N1: Part1.D8, Part2.Trig
  N2: Part1.D9_PWM, Part2.Echo
  5V: Part1.5V, Part2.VCC
  GND: Part1.GND, Part2.GND
